# Fritzing sketch Blackbox (saved by Fritzing 0.9.9b)
breadboards: 1

parts:
  Part1 = Arduino Mega 2560 (Rev3)
  Transceiver1 = nRF24L01 [package=module]
  S1 = Toggle Switch [package=THT]
  S2 = Toggle Switch [package=THT]
  S3 = Toggle Switch [package=THT]
  S4 = Toggle Switch [package=THT]
  S5 = Toggle Switch [package=THT]
  S6 = Toggle Switch [package=THT]
  S7 = Toggle Switch [package=THT]
  S8 = Toggle Switch [package=THT]
  S9 = Pushbutton [package="[THT]"]
  S10 = Pushbutton [package="[THT]"]
  S11 = Pushbutton [package="[THT]"]
  S12 = Pushbutton [package="[THT]"]
  LED1 = RGB LED (com. cathode, rgb) [package="5 mm [THT]"]
  LCM1602_IIC1 = LCM1602 IIC [part_number="LCM1602 IIC" chip_label="LCM1602 IIC" package="DIP (Dual Inline) [THT]"]
  S13 = TILT-SWITCH-SW-200D [package=reed_switch_plastic]
  SD_card_module1 = SD Card Module

nets:
  N1: Part1.D21/SCL, LCM1602_IIC1.SCL
  N2: Part1.D20/SDA, LCM1602_IIC1.SDA
  N3: Part1.D10_PWM, SD_card_module1.CS
  N4: Part1.D8_PWM, Transceiver1.CSN
  VCC: Part1.5V, Transceiver1.VCC, LCM1602_IIC1.VCC
  GND: Part1.GND, Transceiver1.GND, S1.COM, S2.COM, S3.COM, S4.COM, S5.COM, S6.COM, S7.COM, S8.COM, S9.Pin_3, S9.Pin_4, S10.Pin_3, S10.Pin_4, S11.Pin_3, S11.Pin_4, S12.Pin_3, S12.Pin_4, LED1.common_cathode, LCM1602_IIC1.GND, S13.2
  N5: Part1.D7_PWM, Transceiver1.CE
  N6: Part1.D22, S1.L2
  N7: Part1.D23, S2.L2
  N8: Part1.D24, S3.L2
  N9: Part1.D25, S4.L2
  N10: Part1.D26, S5.L2
  N11: Part1.D27, S6.L2
  N12: Part1.D28, S7.L2
  N13: Part1.D29, S8.L2
  N14: Part1.D30, S9.Pin_1, S9.Pin_2
  N15: Part1.D31, S10.Pin_1, S10.Pin_2
  N16: Part1.D32, S11.Pin_1, S11.Pin_2
  N17: Part1.D33, S12.Pin_1, S12.Pin_2
  N18: Part1.D34, LED1.red_anode
  N19: Part1.D35, LED1.green_anode
  N20: Part1.D36, LED1.blue_anode
  N21: Part1.D37, S13.1
  N22: Part1.D50, Transceiver1.MISO
  N23: Part1.D51, Transceiver1.MOSI
  N24: Part1.D52, Transceiver1.SCK

custom parts:
  nRF24L01: nRF24L01 module
  LCM1602 IIC: I2C-Module to use a 1602 or 2004 LCD on with the wire.h libory Serial LCD Modul
  SD Card Module: SD Card Module Slot Socket Reader For Arduino ARM MCU
