# Fritzing sketch Remote (saved by Fritzing 0.9.9b)

parts:
  Part1 = Arduino Mega 2560 (Rev3)
  Transceiver1 = nRF24L01 [package=module]
  LCM1602_IIC1 = LCM1602 IIC [part_number="LCM1602 IIC" chip_label="LCM1602 IIC" package="DIP (Dual Inline) [THT]"]

nets:
  N1: Part1.D21/SCL, LCM1602_IIC1.SCL
  N2: Part1.D20/SDA, LCM1602_IIC1.SDA
  N3: Part1.D8_PWM, Transceiver1.VCC, Transceiver1.CSN
  N4: Part1.D7_PWM, Transceiver1.GND, Transceiver1.CE
  N5: Part1.D50, Transceiver1.MISO
  N6: Part1.D51, Transceiver1.MOSI
  N7: Part1.D52, Transceiver1.SCK

custom parts:
  nRF24L01: nRF24L01 module
  LCM1602 IIC: I2C-Module to use a 1602 or 2004 LCD on with the wire.h libory Serial LCD Modul
