# Fritzing sketch Sentry (saved by Fritzing 0.9.9b)
breadboards: 4

parts:
  Part1 = Arduino Mega 2560 (Rev3)
  PIR1 = PIR sensor
  Transceiver1 = nRF24L01 [package=module]
  SP1 = SPEAKER [package=pcb_mount_speaker]
  SP2 = SPEAKER [package=pcb_mount_speaker]
  LCM1602_IIC1 = LCM1602 IIC [part_number="LCM1602 IIC" chip_label="LCM1602 IIC" package="DIP (Dual Inline) [THT]"]
  Mod1 = ESP32 - CAM
  PIR3 = PIR sensor
  PIR4 = PIR sensor
  PIR5 = PIR sensor
  KY-1 = Keyes Relay [package=THT]
  LED1 = LED - 5mm [color="Red (633nm)" current=0.030 package="5 mm [THT]"]
  LED2 = LED - 5mm [color="Red (633nm)" current=0.030 package="5 mm [THT]"]
  LED3 = LED - 5mm [color="Green (555nm)" current=0.030 package="5 mm [THT]"]
  LED4 = LED - 5mm [color="Green (555nm)" current=0.030 package="5 mm [THT]"]
  R3 = Resistor [tolerance=±5% power=0.25 resistance=220 package=THT]
  R4 = Resistor [tolerance=±5% power=0.25 resistance=220 package=THT]
  R5 = Resistor [tolerance=±5% power=0.25 resistance=220 package=THT]
  LED5 = RGB LED (com. cathode, rgb) [package="5 mm [THT]"]
  R6 = PHOTOCELL [package=photocell]
  R7 = Resistor [tolerance=±5% resistance=1k package="0603 [SMD]"]
  LED6 = LED - 5mm [color="Red (633nm)" current=0.030 package="5 mm [THT]"]
  LED7 = LED - 5mm [color="Red (633nm)" current=0.030 package="5 mm [THT]"]
  LED8 = LED - 5mm [color="Green (555nm)" current=0.030 package="5 mm [THT]"]
  LED9 = LED - 5mm [color="Green (555nm)" current=0.030 package="5 mm [THT]"]
  R8 = Resistor [tolerance=±5% resistance=220 package="0402 [SMD]"]
  R9 = Resistor [tolerance=±5% resistance=220 package="0402 [SMD]"]
  R10 = Resistor [tolerance=±5% resistance=220 package="0402 [SMD]"]
  R11 = Resistor [tolerance=±5% resistance=220 package="0402 [SMD]"]
  R12 = Resistor [tolerance=±5% resistance=220 package="0402 [SMD]"]
  R13 = Resistor [tolerance=±5% resistance=220 package="0402 [SMD]"]
  R14 = Resistor [tolerance=±5% resistance=220 package="0402 [SMD]"]
  R15 = Resistor [tolerance=±5% resistance=220 package="0402 [SMD]"]
  C1 = Electrolytic Capacitor [capacitance=10µF voltage=50V package="1010 [SMD, electrolytic]"]
  KY-2 = Keyes Relay [package=THT]
  R16 = PHOTOCELL [package=photocell]
  R17 = Resistor [tolerance=±5% resistance=1k package="0603 [SMD]"]
  S1 = Pushbutton [package="[THT]"]
  S2 = Pushbutton [package="[THT]"]
  LED10 = LED - 5mm [color="Red (633nm)" current=0.030 package="5 mm [THT]"]
  LED11 = LED - 5mm [color="Red (633nm)" current=0.030 package="5 mm [THT]"]
  LED12 = LED - 5mm [color="Green (555nm)" current=0.030 package="5 mm [THT]"]
  R18 = Resistor [tolerance=±5% power=0.25 resistance=220 package=THT]
  R19 = Resistor [tolerance=±5% power=0.25 resistance=220 package=THT]
  R20 = Resistor [tolerance=±5% power=0.25 resistance=220 package=THT]
  LED13 = LED - 5mm [color="Red (633nm)" current=0.030 package="5 mm [THT]"]
  LED14 = LED - 5mm [color="Red (633nm)" current=0.030 package="5 mm [THT]"]
  LED15 = LED - 5mm [color="Red (633nm)" current=0.030 package="5 mm [THT]"]
  LED16 = LED - 5mm [color="Red (633nm)" current=0.030 package="5 mm [THT]"]
  R22 = Resistor [tolerance=±5% power=0.25 resistance=220 package=THT]
  R23 = Resistor [tolerance=±5% power=0.25 resistance=220 package=THT]
  R24 = Resistor [tolerance=±5% power=0.25 resistance=220 package=THT]
  R25 = Resistor [tolerance=±5% power=0.25 resistance=220 package=THT]
  S3 = Pushbutton [package="[THT]"]
  S4 = Pushbutton [package="[THT]"]
  S5 = Pushbutton [package="[THT]"]
  Part2 = Arduino Uno (Rev3)
  AMP1 = GF1002 Stereo Amplifier
  SD_card_module2 = SD Card Module

nets:
  N1: Part1.A0, R16.P$2, R17.Pin_0
  N2: Part1.A1, R6.P$1, R7.Pin_0
  N3: Part1.D21/SCL, LCM1602_IIC1.SCL, Part2.A5/SCL
  N4: Part1.D20/SDA, LCM1602_IIC1.SDA, Part2.A4/SDA
  GND: Part1.GND, PIR1.GND, Transceiver1.GND, LCM1602_IIC1.GND, Mod1.GND, PIR3.GND, PIR4.GND, PIR5.GND, KY-1.ground, LED1.cathode, C1.-, KY-2.ground, R23.Pin_0, R24.Pin_0, R25.Pin_0, S3.Pin_3, S3.Pin_4, S4.Pin_3, S4.Pin_4, S5.Pin_3, S5.Pin_4
  N5: Part1.D12_PWM, LED13.anode
  N6: Part1.D11_PWM, LED14.anode
  N7: Part1.D9_PWM, LED16.anode
  N8: Part1.D8_PWM, LED15.anode
  3V3: Part1.3V3, Transceiver1.VCC, C1.+
  VDD: Part1.5V, PIR1.VDD, LCM1602_IIC1.VCC, Mod1.VCC, PIR3.VDD, PIR4.VDD, PIR5.VDD, KY-1.power, R6.P$2, KY-2.power, R16.P$1
  N9: Part1.D2_PWM, S5.Pin_1, S5.Pin_2
  N10: Part1.D3_PWM, S4.Pin_1, S4.Pin_2
  N11: Part1.D4_PWM, S3.Pin_1, S3.Pin_2
  N12: Part1.D6_PWM, Transceiver1.CE
  N13: Part1.D7_PWM, Transceiver1.CSN
  N14: Part1.D23, KY-2.signal
  N15: Part1.D24, KY-1.signal
  N16: Part1.D26, PIR3.SIG
  N17: Part1.D27, PIR4.SIG
  N18: Part1.D28, PIR1.SIG
  N19: Part1.D29, PIR5.SIG
  N20: Part1.D32, R8.Pin_0
  N21: Part1.D33, R9.Pin_0
  N22: Part1.D34, R10.Pin_0
  N23: Part1.D35, R11.Pin_0
  N24: Part1.D36, R12.Pin_0
  N25: Part1.D37, R13.Pin_0
  N26: Part1.D38, R14.Pin_0
  N27: Part1.D39, R15.Pin_0
  N28: Part1.D40, R3.Pin_1
  N29: Part1.D41, R4.Pin_1
  N30: Part1.D42, R5.Pin_1
  N31: Part1.D44, LED10.anode
  N32: Part1.D45, LED11.anode
  N33: Part1.D48, S1.Pin_3, S1.Pin_4
  N34: Part1.D49, S2.Pin_3, S2.Pin_4
  N35: Part1.D50, Transceiver1.MISO
  N36: Part1.D51, Transceiver1.MOSI
  N37: Part1.D52, Transceiver1.SCK
  N38: SP1.+, AMP1.ROUT-
  N39: SP1.-, AMP1.ROUT+
  N40: SP2.+, AMP1.LOUT-
  N41: SP2.-, AMP1.LOUT+
  N42: LED1.anode, R8.Pin_1
  N43: LED2.anode, R9.Pin_1
  N44: LED3.anode, R12.Pin_1
  N45: LED4.anode, R13.Pin_1
  N46: R3.Pin_0, LED5.red_anode
  N47: R4.Pin_0, LED5.green_anode
  N48: R5.Pin_0, LED5.blue_anode
  N49: R7.Pin_1, R17.Pin_1, R18.Pin_1, R19.Pin_1, R20.Pin_1
  N50: LED6.anode, R10.Pin_1
  N51: LED7.anode, R11.Pin_1
  N52: LED8.anode, R14.Pin_1
  N53: LED9.anode, R15.Pin_1
  N54: S1.Pin_1, S1.Pin_2
  N55: S2.Pin_1, S2.Pin_2
  N56: LED10.cathode, R18.Pin_0
  N57: LED11.cathode, R20.Pin_0
  N58: LED12.cathode, R19.Pin_0
  N59: LED13.cathode, R25.Pin_1
  N60: LED14.cathode, R24.Pin_1
  N61: LED15.cathode, R22.Pin_1
  N62: LED16.cathode, R23.Pin_1
  N63: Part2.D9_PWM, AMP1.INPUTL, AMP1.INPUTR
  N64: Part2.D11_PWM/MOSI, SD_card_module2.MOSI
  N65: Part2.D12/MISO, SD_card_module2.MISO
  N66: Part2.D13/SCK, SD_card_module2.SCK
  GND_2: Part2.GND, AMP1.POWER-, AMP1.INPUTG, SD_card_module2.GND
  N67: Part2.D4, SD_card_module2.CS
  N68: Part2.5V, AMP1.POWER+, SD_card_module2.+5

notes:
  This component will not be included in the main body of the Sentry. ------->

custom parts:
  nRF24L01: nRF24L01 module
  LCM1602 IIC: I2C-Module to use a 1602 or 2004 LCD on with the wire.h libory Serial LCD Modul
  ESP32 - CAM: The ESP32-CAM has a very competitive small-size camera module that can operate independently as a minimum system with a footprint of only 27*40.5*4.5mm and a deep sleep current of up to 6mA.
  Keyes Relay: The Keyes 5V relay module is suitable for SCM development, home appliance control. It uses a 5V~12V TIL control signal which can control DC / AC signal.
  GF1002 Stereo Amplifier: GF1002 6 Watt Stereo Amplifier
  SD Card Module: SD Card Module Slot Socket Reader For Arduino ARM MCU
